# Fritzing sketch 3-x-x wiring (saved by Fritzing 0.9.6b)

parts:
  Part1 = Adafruit Feather RP2040 [part_number="Adafruit #4884"]
  Part7 = Adafruit DRV8833 DC/Stepper Motor Driver [part_number="Adafruit #3297"]
  Front_Motor1 = DC Motor
  Back_Motor1 = DC Motor
  Part8 = Adafruit VL53L0X Time of Flight Distance Sensor [part_number="Adafruit #3317"]
  U2 = LIPO-110mAh [package=lipo-110]
  S1 = Pushbutton [package=THT]
  Adafruit_VCNL1 = Adafruit VCNL4040
  Front_Right_Light_Sensor = ALSPT19315C
  Front_Left_Light_Sensor = ALSPT19315C
  Rear_Light_Sensor = ALSPT19315C
  Part9 = Adafruit BQ24074 Solar-DC-USB Lipo Charger
  R1 = Resistor [tolerance=±5% power=0.25 resistance=2200 package=THT]
  R2 = Resistor [tolerance=±5% power=0.25 resistance=1000 package=THT]

nets:
  GND: Part1.GND, Part7.GND, Part8.GND, U2.-, Adafruit_VCNL1.GND, Front_Right_Light_Sensor.GND, Front_Left_Light_Sensor.GND, Rear_Light_Sensor.GND, Part9.GND, R1.Pin_1
  VCC: Part1.+3V3, Part8.VIN, S1.leg0, Adafruit_VCNL1.VCC, Front_Right_Light_Sensor.VCC, Front_Left_Light_Sensor.VCC, Rear_Light_Sensor.VCC
  N1: Part1.SDA, Part8.SDA, Adafruit_VCNL1.SDA
  N2: Part1.SCL, Part8.SCL, Adafruit_VCNL1.SCL
  N3: Part1.D25, Part9.!CHG
  N4: Part1.D24, S1.leg1
  N5: Part1.A3, Rear_Light_Sensor.OUT
  N6: Part1.A2, Front_Left_Light_Sensor.OUT
  N7: Part1.A1, Front_Right_Light_Sensor.OUT
  N8: Part1.A0, U2.+, Part9.VLIPO
  N9: Part1.VBAT, Part7.VMOTOR, Part9.OUT
  N10: Part1.D12, Part7.BIN2
  N11: Part1.D11, Part7.BIN1
  N12: Part1.D10, Part7.AIN2
  N13: Part1.D9, Part7.AIN1
  N14: Part7.AOUT2, Back_Motor1.pin_2
  N15: Part7.AOUT1, Back_Motor1.pin_1
  N16: Part7.BOUT1, Front_Motor1.pin_2
  N17: Part7.BOUT2, Front_Motor1.pin_1
  N18: Part9.ISET, R2.Pin_0
  N19: R1.Pin_0, R2.Pin_1

custom parts:
  Adafruit Feather RP2040: A new chip means a new Feather, and the Raspberry Pi RP2040 is no exception. When we saw this chip we thought "this chip is going to be awesome when we give it the Feather Treatment" and so we did! This Feather features the RP2040, and all niceties you know and love about Feather Measures 2.0" x 0.9" x 0.28" (50.8mm x 22.8mm x 7mm) without headers soldered in Light as a (large?) feather - 5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
  Adafruit DRV8833 DC/Stepper Motor Driver: Spin two DC motors or step one bi-polar or uni-polar stepper with up to 1.2A per channel using the DRV8833. This motor driver chip is a nice alternative to the TB6612 driver. Like that chip, you get 2 full H-bridges, but this chip is better for low voltage uses (can run from 2.7V up to 10.8V motor power) and has built in current limiting capability. We set it up for 1A current limiting so you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
  Adafruit VL53L0X Time of Flight Distance Sensor: The VL53L0X is a Time of Flight distance sensor like no other you've used! The sensor contains a very tiny invisible laser source, and a matching sensor. The VL53L0X can detect the "time of flight", or how long the light has taken to bounce back to the sensor. Since it uses a very narrow light source, it is good for determining distance of only the surface directly in front of it. Unlike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
  ALSPT19315C: Add a teeny analog light sensor, the ALS PT19 analog light sensor is a great way to upgrade a project that uses a photocell and needs RoHS compliance. Due to the high rejection ratio of infrared radiation, the spectral response of the ambient light sensor is close to that of human eyes. It's a pretty simple sensor - connect - to ground, + to 2.5V-5.5V or so to power it. Now measure the analog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
