# Fritzing sketch Wiring sketch (saved by Fritzing 0.9.6b)

parts:
  Part5 = Adafruit QT Py [part_number="Adafruit #4600"]
  Part6 = Adafruit DRV8833 DC/Stepper Motor Driver [part_number="Adafruit #3297"]
  Front_Motor = DC Motor
  Back_Motor = DC Motor
  Part7 = Adafruit VL53L0X Time of Flight Distance Sensor [part_number="Adafruit #3317"]
  Part8 = Adafruit Pro Trinket LiIon/LiPoly Backpack [part_number="Adafruit #2124"]
  U2 = SWITCH_SPDT [package=kps-1290]
  D2 = Schottky Diode [part_number=1N5817 package="Melf DO-213 AB [SMD]"]

nets:
  GND: Part5.GND, Part6.GND, Part7.GND, Part8.GND
  3.3V: Part5.3.3V, Part7.VIN
  N1: Part5.SDA, Part7.SDA
  N2: Part5.SCL, Part7.SCL
  N3: Part5.RX_A7, Part6.BIN2
  N4: Part5.SCK, Part6.BIN1
  N5: Part5.MISO, Part6.AIN2
  N6: Part5.MOSI, Part6.AIN1
  N7: Part5.+5V, Part6.VMOTOR, U2.P
  N8: Part6.AOUT2, Back_Motor.pin_2
  N9: Part6.AOUT1, Back_Motor.pin_1
  N10: Part6.BOUT1, Front_Motor.pin_2
  N11: Part6.BOUT2, Front_Motor.pin_1
  N12: Part8.VBUS, U2.S
  N13: Part8.VBAT, D2.anode
  N14: U2.O, D2.cathode

custom parts:
  Adafruit QT Py: What a cutie pie! Or is it... a QT Py? This diminutive dev board comes with our favorite lil chip, the SAMD21 (as made famous in our GEMMA M0 and Trinket M0 boards). This time it comes with our favorite connector - the STEMMA QT, a chainable I2C port that can be used with any of our STEMMA QT sensors and accessories. OLEDs! Inertial Measurment Units! Sensors a-plenty. All plug-and-play thanks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
  Adafruit DRV8833 DC/Stepper Motor Driver: Spin two DC motors or step one bi-polar or uni-polar stepper with up to 1.2A per channel using the DRV8833. This motor driver chip is a nice alternative to the TB6612 driver. Like that chip, you get 2 full H-bridges, but this chip is better for low voltage uses (can run from 2.7V up to 10.8V motor power) and has built in current limiting capability. We set it up for 1A current limiting so you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
  Adafruit VL53L0X Time of Flight Distance Sensor: The VL53L0X is a Time of Flight distance sensor like no other you've used! The sensor contains a very tiny invisible laser source, and a matching sensor. The VL53L0X can detect the "time of flight", or how long the light has taken to bounce back to the sensor. Since it uses a very narrow light source, it is good for determining distance of only the surface directly in front of it. Unlike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
  Adafruit Pro Trinket LiIon/LiPoly Backpack: If you have a Pro Trinket you probably know it's the perfect little size for a portable project. This LiPoly backpack makes it really easy to do! Instead of wiring 2 or 3 boards together to make a charging system, this little PCB sits on top of the Pro Trinket and allows a LiPoly/LiIon battery to plug in. When the Pro Trinket USB port is powered, the battery is recharged automatically. Unplug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
